// Logisim project nand2tetris.circ as structural Verilog: 17 circuits, main circuit main
module main (
);

  // RGB_Video #(.height(256), .width(256)) rgb_video_1: pin names not known
  // RGB_Video #(.height(256), .width(256)) rgb_video_2: pin names not known
endmodule

module ALU16 (
  input  NO,
  input  F,
  input  NY,
  input  ZY,
  input  NX,
  input  ZX,
  input  [15:0] X,
  input  [15:0] Y,
  output ZR,
  output NG,
  output [15:0] OUTP
);

  wire adder_3_cout, undriven_3, undriven_4, undriven_5, undriven_6, undriven_7, undriven_8;
  wire [15:0] adder_1_out, adder_2_out, and_1_out, and_2_out, demultiplexer_1_out0, demultiplexer_1_out1,
       demultiplexer_2_out0, demultiplexer_2_out1, demultiplexer_3_out0, demultiplexer_3_out1,
       demultiplexer_4_out0, demultiplexer_4_out1, demultiplexer_5_out0, demultiplexer_5_out1,
       demultiplexer_6_out0, demultiplexer_6_out1, demultiplexer_7_out0, demultiplexer_7_out1,
       multiplexer_1_out, multiplexer_2_out, multiplexer_3_out, multiplexer_4_out, multiplexer_5_out,
       multiplexer_6_out, multiplexer_7_out, multiplexer_8_out, multiplexer_9_out, multiplexer_11_out,
       multiplexer_12_out, not_1_out, not_2_out, not_3_out, not_4_out, not_5_out, not_6_out, not_7_out,
       not_8_out, undriven, undriven_2, xor_1_out, xor_2_out;

  Demultiplexer #(.width(16)) demultiplexer_1 (
    .out0(demultiplexer_1_out0), .out1(demultiplexer_1_out1), .in(undriven), .sel(undriven_3));
  Demultiplexer #(.width(16)) demultiplexer_2 (
    .out0(demultiplexer_2_out0), .out1(demultiplexer_2_out1), .in(undriven_2), .sel(undriven_4));
  assign not_1_out = ~demultiplexer_1_out1;  // NOT_Gate not_1, 16 bits wide
  assign not_2_out = ~demultiplexer_2_out1;  // NOT_Gate not_2, 16 bits wide
  Multiplexer #(.width(16)) multiplexer_1 (.in0(X), .in1({16{1'b0}}), .out(multiplexer_1_out), .sel(ZX));
  Multiplexer #(.width(16)) multiplexer_2 (.in0(Y), .in1({16{1'b0}}), .out(multiplexer_2_out), .sel(ZY));
  Multiplexer #(.width(16)) multiplexer_3 (
    .in0(demultiplexer_1_out0), .in1(xor_1_out), .out(multiplexer_3_out), .sel(undriven_3));
  assign xor_1_out = not_1_out ^ demultiplexer_1_out1;  // XOR_Gate xor_1, 16 bits wide
  Multiplexer #(.width(16)) multiplexer_4 (
    .in0(demultiplexer_2_out0), .in1(xor_2_out), .out(multiplexer_4_out), .sel(undriven_4));
  assign xor_2_out = not_2_out ^ demultiplexer_2_out1;  // XOR_Gate xor_2, 16 bits wide
  Multiplexer #(.width(16)) multiplexer_5 (.in0(multiplexer_1_out), .in1(not_3_out), .out(multiplexer_5_out), .sel(NX));
  assign not_3_out = ~multiplexer_1_out;  // NOT_Gate not_3, 16 bits wide
  Multiplexer #(.width(16)) multiplexer_6 (.in0(multiplexer_2_out), .in1(not_4_out), .out(multiplexer_6_out), .sel(NY));
  assign not_4_out = ~multiplexer_2_out;  // NOT_Gate not_4, 16 bits wide
  Demultiplexer #(.width(16)) demultiplexer_3 (
    .out0(demultiplexer_3_out0), .out1(demultiplexer_3_out1), .in(multiplexer_3_out), .sel(undriven_5));
  Demultiplexer #(.width(16)) demultiplexer_4 (
    .out0(demultiplexer_4_out0), .out1(demultiplexer_4_out1), .in(multiplexer_4_out), .sel(undriven_6));
  Multiplexer #(.width(16)) multiplexer_7 (
    .in0(demultiplexer_3_out0), .in1(not_5_out), .out(multiplexer_7_out), .sel(undriven_5));
  assign not_5_out = ~demultiplexer_3_out1;  // NOT_Gate not_5, 16 bits wide
  Multiplexer #(.width(16)) multiplexer_8 (
    .in0(demultiplexer_4_out0), .in1(not_6_out), .out(multiplexer_8_out), .sel(undriven_6));
  assign not_6_out = ~demultiplexer_4_out1;  // NOT_Gate not_6, 16 bits wide
  assign and_1_out = multiplexer_5_out & multiplexer_6_out;  // AND_Gate and_1, 16 bits wide
  Adder #(.width(16)) adder_1 (
    .a(multiplexer_5_out), .b(multiplexer_6_out), .out(adder_1_out), .cin(1'b0));  // open: cout
  Demultiplexer #(.width(16)) demultiplexer_5 (
    .out0(demultiplexer_5_out0), .out1(demultiplexer_5_out1), .in(multiplexer_7_out), .sel(undriven_7));
  Demultiplexer #(.width(16)) demultiplexer_6 (
    .out0(demultiplexer_6_out0), .out1(demultiplexer_6_out1), .in(multiplexer_8_out), .sel(undriven_7));
  Multiplexer #(.width(16)) multiplexer_9 (.in0(and_1_out), .in1(adder_1_out), .out(multiplexer_9_out), .sel(F));
  assign not_7_out = ~multiplexer_9_out;  // NOT_Gate not_7, 16 bits wide
  assign and_2_out = demultiplexer_5_out0 & demultiplexer_6_out0;  // AND_Gate and_2, 16 bits wide
  Adder #(.width(16)) adder_2 (
    .a(demultiplexer_5_out1), .b(demultiplexer_6_out1), .out(adder_2_out), .cin(1'b0));  // open: cout
  Multiplexer #(.width(16)) multiplexer_10 (.in0(multiplexer_9_out), .in1(not_7_out), .out({NG, OUTP[14:0]}), .sel(NO));
  Multiplexer #(.width(16)) multiplexer_11 (
    .in0(and_2_out), .in1(adder_2_out), .out(multiplexer_11_out), .sel(undriven_7));
  Demultiplexer #(.width(16)) demultiplexer_7 (
    .out0(demultiplexer_7_out0), .out1(demultiplexer_7_out1), .in(multiplexer_11_out), .sel(undriven_8));
  nor nor_1 (ZR, OUTP[0], OUTP[1], OUTP[2], OUTP[3], OUTP[4], OUTP[5], OUTP[6], OUTP[7], OUTP[8], OUTP[9], OUTP[10], OUTP[11], OUTP[12], OUTP[13], OUTP[14], NG);
  Multiplexer #(.width(16)) multiplexer_12 (
    .in0(demultiplexer_7_out0), .in1(not_8_out), .out(multiplexer_12_out), .sel(undriven_8));
  assign not_8_out = ~demultiplexer_7_out1;  // NOT_Gate not_8, 16 bits wide
  Adder adder_3 (.cout(adder_3_cout));  // open: a, b, out, cin
  Adder adder_4 (.cin(adder_3_cout));  // open: a, b, out, cout

  assign OUTP[15] = NG;

  // Notes on the sheet:
  //   Old Ver.
  //   16-BIT HACK ALU WITH 6-BIT CONTROL
endmodule

module SR_Latch (
  input  S,
  input  R,
  output Q,
  output Q_bar
);

  nand nand_1 (Q, S, Q_bar);
  nand nand_2 (Q_bar, Q, R);
endmodule

module Gated_D_Latch (
  input  D,
  input  Enable,
  output O
);

  wire nand_1_out, nand_2_out, nand_3_out, nand_4_out, nand_5_out, not_1_out, not_2_out, or_1_out, R_out,
       undriven, undriven_2;

  not not_1 (not_1_out, Enable);
  nand nand_1 (nand_1_out, D, Enable);
  or or_1 (or_1_out, D, not_1_out);
  nand S (O, nand_1_out, R_out);
  nand R (R_out, O, or_1_out);
  not not_2 (not_2_out, undriven);
  nand nand_2 (nand_2_out, undriven, undriven_2);
  nand nand_3 (nand_3_out, not_2_out, undriven_2);
  nand nand_4 (nand_4_out, nand_2_out, nand_5_out);
  nand nand_5 (nand_5_out, nand_4_out, nand_3_out);

  // Notes on the sheet:
  //   D
  //   Clock
  //   (NAND gates only)
endmodule

module DFF (
  input  D,
  input  CLK,
  output O
);

  wire nand_1_out, nand_2_out, not_1_out, not_2_out, not_3_out, or_1_out, or_2_out, R0_out, R1_out, S0_out;

  not not_1 (not_1_out, CLK);
  not not_2 (not_2_out, not_1_out);
  nand nand_1 (nand_1_out, D, not_1_out);
  or or_1 (or_1_out, D, not_2_out);
  nand S0 (S0_out, nand_1_out, R0_out);
  nand R0 (R0_out, S0_out, or_1_out);
  not not_3 (not_3_out, CLK);
  nand nand_2 (nand_2_out, S0_out, CLK);
  or or_2 (or_2_out, S0_out, not_3_out);
  nand S1 (O, nand_2_out, R1_out);
  nand R1 (R1_out, O, or_2_out);

  // Notes on the sheet:
  //   Master
  //   Slave
endmodule

module Bit_Register (
  input  INP,
  input  LOAD,
  input  CLK,
  output O
);

  wire multiplexer_1_out;

  Multiplexer multiplexer_1 (.in0(O), .in1(INP), .out(multiplexer_1_out), .sel(LOAD));
  DFF dff_1 (.D(multiplexer_1_out), .CLK(CLK), .O(O));
endmodule

module Register16 (
  input  [15:0] INP,
  input  LOAD,
  input  CLK,
  output [15:0] O
);

  Bit_Register bit_register_1 (.INP(INP[0]), .LOAD(LOAD), .CLK(CLK), .O(O[0]));
  Bit_Register bit_register_2 (.INP(INP[1]), .LOAD(LOAD), .CLK(CLK), .O(O[1]));
  Bit_Register bit_register_3 (.INP(INP[2]), .LOAD(LOAD), .CLK(CLK), .O(O[2]));
  Bit_Register bit_register_4 (.INP(INP[3]), .LOAD(LOAD), .CLK(CLK), .O(O[3]));
  Bit_Register bit_register_5 (.INP(INP[4]), .LOAD(LOAD), .CLK(CLK), .O(O[4]));
  Bit_Register bit_register_6 (.INP(INP[5]), .LOAD(LOAD), .CLK(CLK), .O(O[5]));
  Bit_Register bit_register_7 (.INP(INP[6]), .LOAD(LOAD), .CLK(CLK), .O(O[6]));
  Bit_Register bit_register_8 (.INP(INP[7]), .LOAD(LOAD), .CLK(CLK), .O(O[7]));
  Bit_Register bit_register_9 (.INP(INP[8]), .LOAD(LOAD), .CLK(CLK), .O(O[8]));
  Bit_Register bit_register_10 (.INP(INP[9]), .LOAD(LOAD), .CLK(CLK), .O(O[9]));
  Bit_Register bit_register_11 (.INP(INP[10]), .LOAD(LOAD), .CLK(CLK), .O(O[10]));
  Bit_Register bit_register_12 (.INP(INP[11]), .LOAD(LOAD), .CLK(CLK), .O(O[11]));
  Bit_Register bit_register_13 (.INP(INP[12]), .LOAD(LOAD), .CLK(CLK), .O(O[12]));
  Bit_Register bit_register_14 (.INP(INP[13]), .LOAD(LOAD), .CLK(CLK), .O(O[13]));
  Bit_Register bit_register_15 (.INP(INP[14]), .LOAD(LOAD), .CLK(CLK), .O(O[14]));
  Bit_Register bit_register_16 (.INP(INP[15]), .LOAD(LOAD), .CLK(CLK), .O(O[15]));
endmodule

module RAM8 (
  input  [15:0] INP,
  input  [2:0] ADDR,
  input  LOAD,
  input  CLK,
  output [15:0] O
);

  wire demultiplexer_1_out0, demultiplexer_1_out1, demultiplexer_1_out2, demultiplexer_1_out3,
       demultiplexer_1_out4, demultiplexer_1_out5, demultiplexer_1_out6, demultiplexer_1_out7;
  wire [15:0] register16_1_o, register16_2_o, register16_3_o, register16_4_o, register16_5_o, register16_6_o,
       register16_7_o, register16_8_o;

  Demultiplexer #(.select(3)) demultiplexer_1 (
    .out0(demultiplexer_1_out0), .out1(demultiplexer_1_out1), .out2(demultiplexer_1_out2),
    .out3(demultiplexer_1_out3), .out4(demultiplexer_1_out4), .out5(demultiplexer_1_out5),
    .out6(demultiplexer_1_out6), .out7(demultiplexer_1_out7), .in(LOAD), .sel(ADDR));
  Register16 register16_1 (.INP(INP), .LOAD(demultiplexer_1_out0), .CLK(CLK), .O(register16_1_o));
  Register16 register16_2 (.INP(INP), .LOAD(demultiplexer_1_out1), .CLK(CLK), .O(register16_2_o));
  Register16 register16_3 (.INP(INP), .LOAD(demultiplexer_1_out2), .CLK(CLK), .O(register16_3_o));
  Register16 register16_4 (.INP(INP), .LOAD(demultiplexer_1_out3), .CLK(CLK), .O(register16_4_o));
  Register16 register16_5 (.INP(INP), .LOAD(demultiplexer_1_out4), .CLK(CLK), .O(register16_5_o));
  Register16 register16_6 (.INP(INP), .LOAD(demultiplexer_1_out5), .CLK(CLK), .O(register16_6_o));
  Register16 register16_7 (.INP(INP), .LOAD(demultiplexer_1_out6), .CLK(CLK), .O(register16_7_o));
  Register16 register16_8 (.INP(INP), .LOAD(demultiplexer_1_out7), .CLK(CLK), .O(register16_8_o));
  Multiplexer #(.select(3), .width(16)) multiplexer_1 (
    .in0(register16_1_o), .in1(register16_2_o), .in2(register16_3_o), .in3(register16_4_o),
    .in4(register16_5_o), .in5(register16_6_o), .in6(register16_7_o), .in7(register16_8_o), .out(O),
    .sel(ADDR));
endmodule

module RAM64 (
  input  [15:0] INP,
  input  [5:0] ADDR,
  input  LOAD,
  input  CLK,
  output [15:0] O
);

  wire demultiplexer_1_out0, demultiplexer_1_out1, demultiplexer_1_out2, demultiplexer_1_out3,
       demultiplexer_1_out4, demultiplexer_1_out5, demultiplexer_1_out6, demultiplexer_1_out7;
  wire [15:0] ram8_1_o, ram8_2_o, ram8_3_o, ram8_4_o, ram8_5_o, ram8_6_o, ram8_7_o, ram8_8_o;

  // Probe on ADDR[2:0]
  // Probe on ADDR[5:3]
  Demultiplexer #(.select(3)) demultiplexer_1 (
    .out0(demultiplexer_1_out0), .out1(demultiplexer_1_out1), .out2(demultiplexer_1_out2),
    .out3(demultiplexer_1_out3), .out4(demultiplexer_1_out4), .out5(demultiplexer_1_out5),
    .out6(demultiplexer_1_out6), .out7(demultiplexer_1_out7), .in(LOAD), .sel(ADDR[2:0]));
  RAM8 ram8_1 (.INP(INP), .ADDR(ADDR[5:3]), .LOAD(demultiplexer_1_out0), .CLK(CLK), .O(ram8_1_o));
  RAM8 ram8_2 (.INP(INP), .ADDR(ADDR[5:3]), .LOAD(demultiplexer_1_out1), .CLK(CLK), .O(ram8_2_o));
  RAM8 ram8_3 (.INP(INP), .ADDR(ADDR[5:3]), .LOAD(demultiplexer_1_out2), .CLK(CLK), .O(ram8_3_o));
  RAM8 ram8_4 (.INP(INP), .ADDR(ADDR[5:3]), .LOAD(demultiplexer_1_out3), .CLK(CLK), .O(ram8_4_o));
  RAM8 ram8_5 (.INP(INP), .ADDR(ADDR[5:3]), .LOAD(demultiplexer_1_out4), .CLK(CLK), .O(ram8_5_o));
  RAM8 ram8_6 (.INP(INP), .ADDR(ADDR[5:3]), .LOAD(demultiplexer_1_out5), .CLK(CLK), .O(ram8_6_o));
  RAM8 ram8_7 (.INP(INP), .ADDR(ADDR[5:3]), .LOAD(demultiplexer_1_out6), .CLK(CLK), .O(ram8_7_o));
  RAM8 ram8_8 (.INP(INP), .ADDR(ADDR[5:3]), .LOAD(demultiplexer_1_out7), .CLK(CLK), .O(ram8_8_o));
  Multiplexer #(.select(3), .width(16)) multiplexer_1 (
    .in0(ram8_1_o), .in1(ram8_2_o), .in2(ram8_3_o), .in3(ram8_4_o), .in4(ram8_5_o), .in5(ram8_6_o),
    .in6(ram8_7_o), .in7(ram8_8_o), .out(O), .sel(ADDR[2:0]));

  // Other names for the same wires on the sheet: ADDR_t[2:0] = ADDR[2:0]
endmodule

module INC16 (
  input  [15:0] INP,
  output [15:0] O
);

  Adder #(.width(16)) adder_1 (.a(INP), .b({16{1'b0}}), .out(O), .cin(1'b1));  // open: cout
endmodule

module Counter16 (
  input  [15:0] INP,
  input  LOAD,
  input  RST,
  input  INC,
  input  CLK,
  output [15:0] O
);

  wire and_1_out, and_2_out, and_3_out, not_1_out, not_2_out, not_3_out, or_1_out;
  wire [15:0] inc16_1_o, multiplexer_1_out, multiplexer_2_out;

  not not_1 (not_1_out, LOAD);
  not not_2 (not_2_out, LOAD);
  and and_1 (and_1_out, not_1_out, RST);
  and and_2 (and_2_out, not_2_out, INC);
  not not_3 (not_3_out, and_1_out);
  and and_3 (and_3_out, not_3_out, and_2_out);
  Multiplexer #(.width(16)) multiplexer_1 (.in0(INP), .in1({16{1'b0}}), .out(multiplexer_1_out), .sel(and_1_out));
  Multiplexer #(.width(16)) multiplexer_2 (
    .in0(multiplexer_1_out), .in1(inc16_1_o), .out(multiplexer_2_out), .sel(and_3_out));
  or or_1 (or_1_out, LOAD, and_1_out, and_3_out);
  Register16 register16_1 (.INP(multiplexer_2_out), .LOAD(or_1_out), .CLK(CLK), .O(O));
  INC16 inc16_1 (.INP(O), .O(inc16_1_o));
endmodule

module HACK_CPU (
  input  CLK,
  input  [15:0] INSTRCT,
  input  [15:0] IN_M,
  input  RST,
  output [15:0] OUT_M,
  output WRT_M,
  output [14:0] ADDR_M,
  output [14:0] PRG_CNTR
);

  wire ARITHMETIC_LOGIC_UNIT_ng, ARITHMETIC_LOGIC_UNIT_zr, J0_out, J1_out, J2_out, nor_1_out, not_1_out,
       not_2_out, or_1_out, or_2_out;
  wire [14:0] demultiplexer_1_out0, demultiplexer_1_out1;
  wire [15:0] A_REGISTER_q, bit_extender_1_out, D_REGISTER_q, multiplexer_1_out, multiplexer_2_out,
       PROGRAM_COUNTER_o;

  Demultiplexer #(.width(15)) demultiplexer_1 (
    .out0(demultiplexer_1_out0), .out1({demultiplexer_1_out1[14:4], WRT_M, demultiplexer_1_out1[2:0]}),
    .in(INSTRCT[14:0]), .sel(INSTRCT[15]));
  and J0 (J0_out, demultiplexer_1_out1[0], nor_1_out);
  assign bit_extender_1_out = {{1{1'b0}}, demultiplexer_1_out0};  // Bit_Extender bit_extender_1
  not not_1 (not_1_out, INSTRCT[15]);
  Multiplexer #(.width(16)) multiplexer_1 (
    .in0(bit_extender_1_out), .in1(OUT_M), .out(multiplexer_1_out), .sel(demultiplexer_1_out1[5]));
  or or_1 (or_1_out, demultiplexer_1_out1[5], not_1_out);
  // Probe on demultiplexer_1_out1[12]
  and J1 (J1_out, demultiplexer_1_out1[1], ARITHMETIC_LOGIC_UNIT_zr);
  Register #(.width(16)) A_REGISTER (.D(multiplexer_1_out), .en(or_1_out), .clk(CLK), .Q(A_REGISTER_q), .clr(RST));
  // Probe on demultiplexer_1_out1[2:0]
  // Probe on {demultiplexer_1_out1[5:4], WRT_M}
  // Probe on demultiplexer_1_out1[11:6]
  and J2 (J2_out, demultiplexer_1_out1[2], ARITHMETIC_LOGIC_UNIT_ng);
  nor nor_1 (nor_1_out, ARITHMETIC_LOGIC_UNIT_ng, ARITHMETIC_LOGIC_UNIT_zr);
  or or_2 (or_2_out, J2_out, J1_out, J0_out);
  not not_2 (not_2_out, or_2_out);
  Register #(.width(16)) D_REGISTER (.D(OUT_M), .en(demultiplexer_1_out1[4]), .clk(CLK), .Q(D_REGISTER_q), .clr(RST));
  Multiplexer #(.width(16)) multiplexer_2 (
    .in0(A_REGISTER_q), .in1(IN_M), .out(multiplexer_2_out), .sel(demultiplexer_1_out1[12]));
  Counter16 PROGRAM_COUNTER (
    .INP(A_REGISTER_q), .LOAD(or_2_out), .RST(RST), .INC(not_2_out), .CLK(CLK), .O(PROGRAM_COUNTER_o));
  ALU16 ARITHMETIC_LOGIC_UNIT (
    .NO(demultiplexer_1_out1[6]), .F(demultiplexer_1_out1[7]), .NY(demultiplexer_1_out1[8]),
    .ZY(demultiplexer_1_out1[9]), .NX(demultiplexer_1_out1[10]), .ZX(demultiplexer_1_out1[11]),
    .X(D_REGISTER_q), .Y(multiplexer_2_out), .ZR(ARITHMETIC_LOGIC_UNIT_zr), .NG(ARITHMETIC_LOGIC_UNIT_ng),
    .OUTP(OUT_M));
  Bit_Extender #(.in_width(16), .out_width(15), .\type ("zero")) bit_extender_2 (.in(A_REGISTER_q), .out(ADDR_M));
  Bit_Extender #(.in_width(16), .out_width(15), .\type ("zero")) bit_extender_3 (
    .in(PROGRAM_COUNTER_o), .out(PRG_CNTR));

  // Notes on the sheet:
  //   j
  //   d
  //   c
  //   a
endmodule

module MEMORY16 (
  input  [15:0] IN_KBD,
  input  [15:0] IN_M,
  input  [14:0] ADDR_M,
  input  LOAD,
  input  CLK,
  output [15:0] OUT_SCRN,
  output [15:0] OUT_M
);

  wire and_1_out, and_2_out, and_3_out, comparator_1_lt, nor_1_out, undriven, xor_1_out;
  wire [12:0] bit_extender_1_out, demultiplexer_2_out0;
  wire [13:0] demultiplexer_1_out0, demultiplexer_1_out1;
  wire [15:0] DATA_RAM_dout, KBD_q;

  // Probe on ADDR_M
  Demultiplexer #(.width(14)) demultiplexer_1 (
    .out0(demultiplexer_1_out0), .out1(demultiplexer_1_out1), .in(ADDR_M[13:0]), .sel(ADDR_M[14]));
  nor nor_1 (nor_1_out, ADDR_M[14], demultiplexer_1_out1[13]);
  and and_1 (and_1_out, nor_1_out, LOAD);
  RAM #(.addrWidth(14), .dataWidth(16)) DATA_RAM (
    .addr(demultiplexer_1_out0), .we(and_1_out), .oe(nor_1_out), .clk(CLK), .din(IN_M), .dout(DATA_RAM_dout));
  assign OUT_M = nor_1_out ? DATA_RAM_dout : 16'bz;  // Controlled_Buffer controlled_buffer_1
  Demultiplexer #(.width(13)) demultiplexer_2 (
    .out0(demultiplexer_2_out0), .in(demultiplexer_1_out1[12:0]), .sel(demultiplexer_1_out1[13]));  // open: out1
  xor xor_1 (xor_1_out, demultiplexer_1_out1[13], ADDR_M[14]);
  RAM #(.addrWidth(13), .dataWidth(16), .enables("line")) SCREEN (
    .addr(demultiplexer_2_out0), .we(and_2_out), .clk(CLK), .din(IN_M), .dout(OUT_SCRN));
  and and_2 (and_2_out, xor_1_out, LOAD);
  assign OUT_M = xor_1_out ? OUT_SCRN : 16'bz;  // Controlled_Buffer controlled_buffer_2
  and and_3 (and_3_out, demultiplexer_1_out1[13], ADDR_M[14]);
  Register #(.width(16)) KBD (.D(IN_KBD), .en(1'b1), .clk(CLK), .Q(KBD_q), .clr(undriven));
  // NoConnect on undriven
  assign bit_extender_1_out = {{12{1'b0}}, and_3_out};  // Bit_Extender bit_extender_1
  assign OUT_M = comparator_1_lt ? KBD_q : 16'bz;  // Controlled_Buffer controlled_buffer_3
  Comparator #(.width(13)) comparator_1 (
    .a(ADDR_M[12:0]), .b(bit_extender_1_out), .lt(comparator_1_lt));  // open: gt, eq
  // Probe on ADDR_M[12:0]

  // Notes on the sheet:
  //   RAM
  //   VRAM
  //   Memory Bus
  //   Keyboard Register
endmodule

module MEM16 (
  input  [15:0] IN_KBD,
  input  [15:0] IN_M,
  input  LOAD,
  input  [14:0] ADDR_M,
  input  [12:0] ADDR_V,
  input  CLK,
  output DISP_DRV_EN,
  output [15:0] OUT_SCRN,
  output [15:0] OUT_M
);

  wire and_1_out, comparator_1_lt, demultiplexer_1_out0, demultiplexer_1_out1, demultiplexer_1_out2,
       not_1_out, or_1_out;
  wire [12:0] multiplexer_1_out;
  wire [15:0] controlled_buffer_1_out, DATA_RAM_dout, KBD_q;

  and and_1 (and_1_out, ~ADDR_M[13], ADDR_M[14]);  // AND_Gate
  // Probe on ADDR_M
  Demultiplexer #(.select(2)) demultiplexer_1 (
    .out0(demultiplexer_1_out0), .out1(demultiplexer_1_out1), .out2(demultiplexer_1_out2), .in(LOAD),
    .sel(ADDR_M[14:13]));  // open: out3
  Multiplexer #(.width(13)) multiplexer_1 (.in0(ADDR_V), .in1(ADDR_M[12:0]), .out(multiplexer_1_out), .sel(and_1_out));
  RAM #(.addrWidth(14), .dataWidth(16), .enables("line")) DATA_RAM (
    .addr(ADDR_M[13:0]), .we(or_1_out), .clk(CLK), .din(IN_M), .dout(DATA_RAM_dout));
  or or_1 (or_1_out, demultiplexer_1_out0, demultiplexer_1_out1);
  Comparator #(.width(13)) comparator_1 (.a({13{1'b0}}), .b(ADDR_M[12:0]), .lt(comparator_1_lt));  // open: gt, eq
  not not_1 (not_1_out, comparator_1_lt);
  RAM #(.addrWidth(13), .dataWidth(16), .enables("line")) VRAM (
    .addr(multiplexer_1_out), .we(demultiplexer_1_out2), .clk(CLK), .din(IN_M), .dout(OUT_SCRN));
  Register #(.width(16)) KBD (.D(IN_KBD), .en(1'b1), .clk(CLK), .Q(KBD_q));  // open: clr
  assign controlled_buffer_1_out = not_1_out ? KBD_q : 16'bz;  // Controlled_Buffer controlled_buffer_1
  not not_2 (DISP_DRV_EN, and_1_out);
  Multiplexer #(.select(2), .width(16)) multiplexer_2 (
    .in0(DATA_RAM_dout), .in1(DATA_RAM_dout), .in2(OUT_SCRN), .in3(controlled_buffer_1_out), .out(OUT_M),
    .sel(ADDR_M[14:13]));
endmodule

module DISP_DRIVER (
  input  [15:0] IN_M,
  input  [12:0] ADDR,
  input  in_3,
  input  in_4,
  output [15:0] OUT_SCRN
);

  RAM #(.addrWidth(13), .dataWidth(16), .enables("line")) VRAM (
    .addr(ADDR), .we(in_3), .clk(in_4), .din(IN_M), .dout(OUT_SCRN));
endmodule

module HACK_CPU_SIMPLE (
  input  CLK,
  input  [15:0] INSTRCT,
  input  [15:0] IN_M,
  input  RST,
  output [15:0] OUT_M,
  output WRT_M,
  output [14:0] ADDR_M,
  output [14:0] PRG_CNTR
);

  wire A, and_1_out, and_2_out, and_3_out, and_5_out, ARITHMETIC_LOGIC_UNIT_ng, ARITHMETIC_LOGIC_UNIT_zr,
       J0_out, J1_out, J2_out, nor_1_out, not_2_out, or_1_out, or_2_out;
  wire [15:0] A_REG, D_REGISTER_q, multiplexer_1_out, multiplexer_2_out, PROGRAM_COUNTER_q;

  not not_1 (A, INSTRCT[15]);
  and J0 (J0_out, and_1_out, nor_1_out);
  and and_1 (and_1_out, INSTRCT[15], INSTRCT[0]);
  and J1 (J1_out, INSTRCT[1], ARITHMETIC_LOGIC_UNIT_zr);
  Multiplexer #(.width(16)) multiplexer_1 (.in0(INSTRCT), .in1(OUT_M), .out(multiplexer_1_out), .sel(INSTRCT[15]));
  or or_1 (or_1_out, INSTRCT[5], A);
  // Probe on INSTRCT[12]
  and J2 (J2_out, INSTRCT[2], ARITHMETIC_LOGIC_UNIT_ng);
  Register #(.width(16)) A_REGISTER (.D(multiplexer_1_out), .en(or_1_out), .clk(CLK), .Q(A_REG), .clr(RST));
  // Probe on INSTRCT[2:0]
  // Probe on INSTRCT[5:3]
  // Probe on INSTRCT[11:6]
  nor nor_1 (nor_1_out, ARITHMETIC_LOGIC_UNIT_ng, ARITHMETIC_LOGIC_UNIT_zr);
  or or_2 (or_2_out, J2_out, J1_out, J0_out);
  and and_2 (and_2_out, or_2_out, INSTRCT[15]);
  not not_2 (not_2_out, and_2_out);
  and and_3 (and_3_out, INSTRCT[4], INSTRCT[15]);
  Register #(.width(16)) D_REGISTER (.D(OUT_M), .en(and_3_out), .clk(CLK), .Q(D_REGISTER_q), .clr(RST));
  Counter #(.max('hffff), .width(16)) PROGRAM_COUNTER (
    .clr(RST), .load(and_2_out), .up(not_2_out), .count(not_2_out), .clk(CLK), .D(A_REG),
    .Q(PROGRAM_COUNTER_q));  // open: carry
  and and_4 (WRT_M, INSTRCT[3], INSTRCT[15]);
  Multiplexer #(.width(16)) multiplexer_2 (.in0(A_REG), .in1(IN_M), .out(multiplexer_2_out), .sel(and_5_out));
  and and_5 (and_5_out, INSTRCT[12], INSTRCT[15]);
  Bit_Extender #(.in_width(16), .out_width(15), .\type ("zero")) bit_extender_1 (.in(A_REG), .out(ADDR_M));
  Bit_Extender #(.in_width(16), .out_width(15), .\type ("zero")) bit_extender_2 (
    .in(PROGRAM_COUNTER_q), .out(PRG_CNTR));
  ALU16 ARITHMETIC_LOGIC_UNIT (
    .NO(INSTRCT[6]), .F(INSTRCT[7]), .NY(INSTRCT[8]), .ZY(INSTRCT[9]), .NX(INSTRCT[10]), .ZX(INSTRCT[11]),
    .X(D_REGISTER_q), .Y(multiplexer_2_out), .ZR(ARITHMETIC_LOGIC_UNIT_zr), .NG(ARITHMETIC_LOGIC_UNIT_ng),
    .OUTP(OUT_M));

  // Other names for the same wires on the sheet: C = INSTRCT[15]

  // Notes on the sheet:
  //   j
  //   d
  //   c
  //   a
endmodule

module HACK_COMPUTER (
  input  [15:0] IN_KBD,
  input  [12:0] ADDR_V,
  input  RST,
  output DISP_DRV_EN,
  output [15:0] OUT_SCRN
);

  wire clock_1_out, CPU_wrt_m;
  wire [14:0] CPU_addr_m, CPU_prg_cntr;
  wire [15:0] CPU_out_m, RAM_VRAM_KBD_out_m, ROM32K_data;

  ROM #(.addrWidth(15), .dataWidth(16)) ROM32K (.addr(CPU_prg_cntr), .data(ROM32K_data));
  Clock clock_1 (.out(clock_1_out));
  // Probe on ROM32K_data
  HACK_CPU_SIMPLE CPU (
    .CLK(clock_1_out), .INSTRCT(ROM32K_data), .IN_M(RAM_VRAM_KBD_out_m), .RST(RST), .OUT_M(CPU_out_m),
    .WRT_M(CPU_wrt_m), .ADDR_M(CPU_addr_m), .PRG_CNTR(CPU_prg_cntr));
  // Probe on CPU_prg_cntr
  // Probe on CPU_addr_m
  // Probe on CPU_out_m
  MEM16 RAM_VRAM_KBD (
    .IN_KBD(IN_KBD), .IN_M(CPU_out_m), .LOAD(CPU_wrt_m), .ADDR_M(CPU_addr_m), .ADDR_V(ADDR_V),
    .CLK(clock_1_out), .DISP_DRV_EN(DISP_DRV_EN), .OUT_SCRN(OUT_SCRN), .OUT_M(RAM_VRAM_KBD_out_m));
  // RGB_Video #(.height(256), .scale(1), .width(256)) rgb_video_1: pin names not known
  // RGB_Video #(.height(256), .scale(1), .width(256)) rgb_video_2: pin names not known

  // Notes on the sheet:
  //   contents of ROM32K (hex, n*v repeats v):
  //   a ec10 10 e388 1 ec10 11 e308 12 efc8 ede0 efc8 11 fc10 10 f4d0 20 e302 11 fc10 12 e0a0 fc10 eca0
  //   f090 ede0 ede0 e308 11 fdc8 c ea87 20 ea87
endmodule
